// Logisim project 1.circ as structural Verilog: 1 circuit, main circuit main
module main (
  input  A,
  input  B,
  input  D4,
  input  D3,
  input  D2,
  input  D1
);

  wire and_1_out, and_2_out, and_3_out, and_4_out, not_1_out, not_2_out, or_1_out;

  not not_1 (not_1_out, A);
  not not_2 (not_2_out, B);
  and and_1 (and_1_out, D4, B, A);
  and and_2 (and_2_out, D3, A, not_2_out);
  and and_3 (and_3_out, D2, B, not_1_out);
  and and_4 (and_4_out, D1, not_2_out, not_1_out);
  or or_1 (or_1_out, and_1_out, and_2_out, and_3_out, and_4_out);
  LED led_1 (.in(or_1_out));
endmodule
