// Logisim project FullAdder.circ as structural Verilog: 1 circuit, main circuit main
module main (
  input  C,
  input  [1:0] B
);

  wire multiplexer_1_out, multiplexer_2_out, not_1_out;

  not not_1 (not_1_out, C);
  Multiplexer #(.select(2), .enable("false")) multiplexer_1 (
    .in0(C), .in1(not_1_out), .in2(not_1_out), .in3(C), .out(multiplexer_1_out), .sel(B));
  Multiplexer #(.select(2), .enable("false")) multiplexer_2 (
    .in0(1'b0), .in1(C), .in2(C), .in3(1'b1), .out(multiplexer_2_out), .sel(B));
  LED led_1 (.in(multiplexer_1_out));
  LED led_2 (.in(multiplexer_2_out));

  // Notes on the sheet:
  //   A
  //   R
  //   Carry out
endmodule
