// Logisim project Multiplicador Complementos a 2.circ as structural Verilog: 1 circuit, main circuit main
module main (
  input  in_1,
  input  in_2,
  input  in_3,
  input  in_4,
  input  in_5,
  input  in_6,
  input  B2,
  input  B3
);

  wire and_2_out, and_3_out, and_4_out, and_5_out, and_6_out, and_7_out, and_8_out, and_9_out, and_10_out,
       and_11_out, and_12_out, and_13_out, and_14_out, and_15_out, and_16_out, and_17_out, and_18_out,
       and_19_out, and_20_out, and_21_out, and_22_out, and_23_out, and_24_out, and_25_out, and_26_out,
       and_27_out, and_28_out, and_29_out, and_30_out, and_31_out, and_32_out, and_33_out, and_34_out,
       and_35_out, and_36_out, and_37_out, and_38_out, and_39_out, and_40_out, and_41_out, nand_1_out,
       nand_2_out, nand_3_out, nand_4_out, nand_5_out, nand_6_out, or_1_out, or_2_out, or_3_out, or_4_out,
       or_5_out, or_6_out, or_7_out, or_8_out, or_9_out, xor_1_out, xor_2_out, xor_3_out, xor_4_out,
       xor_5_out, xor_6_out, xor_7_out, xor_8_out, xor_9_out, xor_10_out, xor_11_out, xor_12_out, xor_13_out,
       xor_14_out, xor_15_out, xor_16_out, xor_17_out, xor_18_out, xor_19_out, xor_20_out, xor_21_out,
       xor_22_out;

  // AND_Gate and_1 has open pins: in0=or_1_out, in1=1'b1, out=open
  xor xor_1 (xor_1_out, 1'b1, or_1_out);
  LED led_1 (.in(xor_1_out));
  and and_2 (and_2_out, or_2_out, and_5_out);
  and and_3 (and_3_out, or_3_out, or_2_out);
  and and_4 (and_4_out, or_3_out, and_5_out);
  or or_1 (or_1_out, and_2_out, and_3_out, and_4_out);
  and and_5 (and_5_out, in_1, B3);
  xor xor_2 (xor_2_out, and_5_out, or_2_out);
  and and_6 (and_6_out, or_4_out, nand_1_out);
  and and_7 (and_7_out, or_5_out, or_4_out);
  or or_2 (or_2_out, and_6_out, and_7_out, and_8_out);
  xor xor_3 (xor_3_out, or_3_out, xor_2_out);
  LED led_2 (.in(xor_3_out));
  and and_8 (and_8_out, or_5_out, nand_1_out);
  and and_9 (and_9_out, nand_2_out, xor_5_out);
  nand nand_1 (nand_1_out, in_1, B2);
  xor xor_4 (xor_4_out, nand_1_out, or_4_out);
  and and_10 (and_10_out, or_6_out, nand_2_out);
  or or_3 (or_3_out, and_9_out, and_10_out, and_11_out);
  xor xor_5 (xor_5_out, or_5_out, xor_4_out);
  and and_11 (and_11_out, or_6_out, xor_5_out);
  and and_12 (and_12_out, 1'b1, nand_3_out);
  and and_13 (and_13_out, or_7_out, 1'b1);
  or or_4 (or_4_out, and_12_out, and_13_out, and_14_out);
  nand nand_2 (nand_2_out, in_2, B3);
  xor xor_6 (xor_6_out, xor_5_out, nand_2_out);
  and and_14 (and_14_out, or_7_out, nand_3_out);
  and and_15 (and_15_out, and_20_out, xor_9_out);
  xor xor_7 (xor_7_out, or_6_out, xor_6_out);
  LED led_3 (.in(xor_7_out));
  nand nand_3 (nand_3_out, in_1, in_6);
  and and_16 (and_16_out, or_8_out, xor_9_out);
  and and_17 (and_17_out, or_8_out, and_20_out);
  or or_5 (or_5_out, and_15_out, and_17_out, and_16_out);
  and and_18 (and_18_out, nand_4_out, xor_11_out);
  xor xor_8 (xor_8_out, nand_3_out, 1'b1);
  xor xor_9 (xor_9_out, or_7_out, xor_8_out);
  and and_19 (and_19_out, and_29_out, nand_4_out);
  or or_6 (or_6_out, and_18_out, and_19_out, and_21_out);
  and and_20 (and_20_out, in_2, B2);
  xor xor_10 (xor_10_out, xor_9_out, and_20_out);
  and and_21 (and_21_out, and_29_out, xor_11_out);
  and and_22 (and_22_out, nand_5_out, and_27_out);
  xor xor_11 (xor_11_out, or_8_out, xor_10_out);
  xor xor_12 (xor_12_out, xor_11_out, nand_4_out);
  and and_23 (and_23_out, or_9_out, and_27_out);
  and and_24 (and_24_out, or_9_out, nand_5_out);
  or or_7 (or_7_out, and_22_out, and_24_out, and_23_out);
  and and_25 (and_25_out, and_30_out, xor_15_out);
  nand nand_4 (nand_4_out, in_3, B3);
  xor xor_13 (xor_13_out, and_29_out, xor_12_out);
  LED led_4 (.in(xor_13_out));
  and and_26 (and_26_out, and_34_out, and_30_out);
  or or_8 (or_8_out, and_25_out, and_26_out, and_28_out);
  nand nand_5 (nand_5_out, in_1, in_5);
  and and_27 (and_27_out, in_2, in_6);
  xor xor_14 (xor_14_out, and_27_out, nand_5_out);
  and and_28 (and_28_out, and_34_out, xor_15_out);
  and and_29 (and_29_out, nand_6_out, xor_18_out);
  xor xor_15 (xor_15_out, or_9_out, xor_14_out);
  and and_30 (and_30_out, in_3, B2);
  xor xor_16 (xor_16_out, xor_15_out, and_30_out);
  nand nand_6 (nand_6_out, in_4, B3);
  xor xor_17 (xor_17_out, nand_6_out, xor_18_out);
  LED led_5 (.in(xor_17_out));
  and and_31 (and_31_out, and_35_out, and_36_out);
  xor xor_18 (xor_18_out, and_34_out, xor_16_out);
  and and_32 (and_32_out, and_38_out, and_35_out);
  or or_9 (or_9_out, and_31_out, and_32_out, and_33_out);
  and and_33 (and_33_out, and_38_out, and_36_out);
  and and_34 (and_34_out, and_37_out, xor_21_out);
  and and_35 (and_35_out, in_2, in_5);
  and and_36 (and_36_out, in_3, in_6);
  xor xor_19 (xor_19_out, and_36_out, and_35_out);
  and and_37 (and_37_out, in_4, B2);
  xor xor_20 (xor_20_out, and_37_out, xor_21_out);
  LED led_6 (.in(xor_20_out));
  xor xor_21 (xor_21_out, and_38_out, xor_19_out);
  and and_38 (and_38_out, and_40_out, and_39_out);
  and and_39 (and_39_out, in_3, in_5);
  and and_40 (and_40_out, in_4, in_6);
  xor xor_22 (xor_22_out, and_40_out, and_39_out);
  LED led_7 (.in(xor_22_out));
  and and_41 (and_41_out, in_4, in_5);
  LED led_8 (.in(and_41_out));

  // Other names for the same wires on the sheet: A0 = in_4; A1 = in_3; A2 = in_2; A3 = in_1

  // Notes on the sheet:
  //   Z7
  //   Z6
  //   Z5
  //   Z4
  //   A3
  //   Z3
  //   A2
  //   Z2
  //   A1
  //   Z1
  //   A0
  //   Z0
  //   B0
  //   B1
endmodule
