// Logisim project Contador99 Ascendente y Descendente.circ as structural Verilog: 1 circuit, main circuit main
module main (
  input  X
);

  wire and_1_out, and_2_out, and_3_out, and_4_out, and_5_out, and_6_out, and_7_out, and_8_out, and_9_out,
       and_10_out, and_11_out, and_12_out, and_13_out, and_14_out, and_15_out, and_16_out, and_17_out,
       and_18_out, and_19_out, and_20_out, and_21_out, and_22_out, and_23_out, and_24_out, and_25_out,
       and_26_out, and_27_out, and_28_out, clock_1_out, EN, J1, J1D, J2, J2D, J3, J3D, K1, K1D, K2, K2D, K3,
       K3D, Q0, Q0D, Q0N, Q0ND, Q1, Q1D, Q1N, Q1ND, Q2, Q2D, Q2N, Q2ND, Q3, Q3D, Q3N, Q3ND, XN;

  not not_1 (XN, X);
  Clock clock_1 (.out(clock_1_out));
  DotMatrix #(.matrixcols(4), .matrixrows(1)) dotmatrix_1 (.col0(Q0), .col1(Q1), .col2(Q2), .col3(Q3));
  and and_1 (and_1_out, Q0, Q1N, Q2N, Q3, XN);
  and and_2 (and_2_out, X, Q0N, Q1N, Q2N, Q3N);
  DotMatrix #(.matrixcols(4), .matrixrows(1)) dotmatrix_2 (.col0(Q0D), .col1(Q1D), .col2(Q2D), .col3(Q3D));
  or or_1 (EN, and_1_out, and_2_out);
  J_K_Flip_Flop j_k_ff_1 (.J(1'b1), .clk(clock_1_out), .K(1'b1), .Q(Q0), .Qn(Q0N));  // open: preset, en, reset
  and and_3 (and_3_out, XN, Q3N, Q0);
  and and_4 (and_4_out, X, Q2, Q0N);
  and and_5 (and_5_out, X, Q3, Q0N);
  J_K_Flip_Flop j_k_ff_2 (.J(1'b1), .clk(clock_1_out), .K(1'b1), .Q(Q0D), .Qn(Q0ND), .en(EN));  // open: preset, reset
  or or_2 (J1, and_4_out, and_3_out, and_5_out);
  and and_6 (and_6_out, XN, Q0);
  and and_7 (and_7_out, X, Q0N);
  and and_8 (and_8_out, XN, Q3ND, Q0D);
  and and_9 (and_9_out, X, Q2D, Q0ND);
  and and_10 (and_10_out, X, Q3D, Q0ND);
  and and_11 (and_11_out, XN, Q0D);
  and and_12 (and_12_out, X, Q0ND);
  J_K_Flip_Flop j_k_ff_3 (.J(J1), .clk(clock_1_out), .K(K1), .Q(Q1), .Qn(Q1N));  // open: preset, en, reset
  or or_3 (K1, and_6_out, and_7_out);
  or or_4 (J1D, and_9_out, and_8_out, and_10_out);
  J_K_Flip_Flop j_k_ff_4 (.J(J1D), .clk(clock_1_out), .K(K1D), .Q(Q1D), .Qn(Q1ND), .en(EN));  // open: preset, reset
  or or_5 (K1D, and_11_out, and_12_out);
  and and_13 (and_13_out, XN, Q1, Q0);
  and and_14 (and_14_out, X, Q3, Q0N);
  J_K_Flip_Flop j_k_ff_5 (.J(J2), .clk(clock_1_out), .K(K2), .Q(Q2), .Qn(Q2N));  // open: preset, en, reset
  and and_15 (and_15_out, XN, Q1, Q0);
  and and_16 (and_16_out, X, Q1N, Q0N);
  and and_17 (and_17_out, XN, Q1D, Q0D);
  and and_18 (and_18_out, X, Q3D, Q0ND);
  and and_19 (and_19_out, XN, Q1D, Q0D);
  and and_20 (and_20_out, X, Q1ND, Q0ND);
  or or_6 (J2, and_13_out, and_14_out);
  or or_7 (K2, and_15_out, and_16_out);
  or or_8 (J2D, and_17_out, and_18_out);
  J_K_Flip_Flop j_k_ff_6 (.J(J2D), .clk(clock_1_out), .K(K2D), .Q(Q2D), .Qn(Q2ND), .en(EN));  // open: preset, reset
  or or_9 (K2D, and_19_out, and_20_out);
  and and_21 (and_21_out, XN, Q0, Q1, Q2);
  and and_22 (and_22_out, X, Q0N, Q1N, Q2N);
  J_K_Flip_Flop j_k_ff_7 (.J(J3), .clk(clock_1_out), .K(K3), .Q(Q3), .Qn(Q3N));  // open: preset, en, reset
  and and_23 (and_23_out, XN, Q0);
  and and_24 (and_24_out, X, Q0N);
  and and_25 (and_25_out, XN, Q0D, Q1D, Q2D);
  and and_26 (and_26_out, X, Q0ND, Q1ND, Q2ND);
  or or_10 (J3, and_21_out, and_22_out);
  or or_11 (K3, and_23_out, and_24_out);
  or or_12 (J3D, and_25_out, and_26_out);
  J_K_Flip_Flop j_k_ff_8 (.J(J3D), .clk(clock_1_out), .K(K3D), .Q(Q3D), .Qn(Q3ND), .en(EN));  // open: preset, reset
  and and_27 (and_27_out, XN, Q0D);
  and and_28 (and_28_out, X, Q0ND);
  or or_13 (K3D, and_27_out, and_28_out);
endmodule
