// Logisim project Controlador.circ as structural Verilog: 1 circuit, main circuit main
module main (
  output out_1,
  output out_2,
  output out_3,
  output out_4
);

  wire and_1_out, clock_1_out, d_ff_2_qn, d_ff_3_qn, d_ff_4_qn;

  Clock clock_1 (.out(clock_1_out));
  D_Flip_Flop #(.trigger("falling")) d_ff_1 (
    .clk(clock_1_out), .D(and_1_out), .Q(out_1));  // open: Qn, preset, en, reset
  and and_1 (and_1_out, d_ff_2_qn, d_ff_3_qn, d_ff_4_qn);
  D_Flip_Flop #(.trigger("falling")) d_ff_2 (
    .clk(clock_1_out), .D(out_1), .Q(out_2), .Qn(d_ff_2_qn));  // open: preset, en, reset
  D_Flip_Flop #(.trigger("falling")) d_ff_3 (
    .clk(clock_1_out), .D(out_2), .Q(out_3), .Qn(d_ff_3_qn));  // open: preset, en, reset
  D_Flip_Flop #(.trigger("falling")) d_ff_4 (
    .clk(clock_1_out), .D(out_3), .Q(out_4), .Qn(d_ff_4_qn));  // open: preset, en, reset

  // Notes on the sheet:
  //   C
  //   B
  //   A
endmodule
