// Logisim project Diseño Final.circ as structural Verilog: 1 circuit, main circuit main
module main (
  input  [3:0] in_1,
  input  [3:0] in_2,
  input  [3:0] in_3,
  input  [3:0] in_4
);

  wire clock_1_out, j_k_ff_1_qn, j_k_ff_2_qn, j_k_ff_3_qn, j_k_ff_4_qn, Q0, Q1, Q2, Q3;
  wire [1:0] or_2_out;
  wire [3:0] multiplexer_1_out;
  wire [6:0] main_1_out_2, Seg1, Seg2, Seg3, Seg4;

  Clock clock_1 (.out(clock_1_out));
  J_K_Flip_Flop j_k_ff_1 (
    .J(Q1), .clk(clock_1_out), .K(j_k_ff_4_qn), .Q(Q0), .Qn(j_k_ff_1_qn));  // open: preset, en, reset
  J_K_Flip_Flop j_k_ff_2 (
    .J(1'b1), .clk(clock_1_out), .K(j_k_ff_1_qn), .Q(Q1), .Qn(j_k_ff_2_qn));  // open: preset, en, reset
  _7_Segment_Display u_7_segment_display_1 (
    .g(Seg1[6]), .f(Seg1[5]), .a(Seg1[0]), .b(Seg1[1]), .e(Seg1[4]), .d(Seg1[3]), .c(Seg1[2]));  // open: dp
  J_K_Flip_Flop j_k_ff_3 (
    .J(1'b1), .clk(clock_1_out), .K(j_k_ff_2_qn), .Q(Q2), .Qn(j_k_ff_3_qn));  // open: preset, en, reset
  DotMatrix #(.matrixcols(4), .matrixrows(1)) dotmatrix_1 (.col0(Q0), .col1(Q1), .col2(Q2), .col3(Q3));
  _7_Segment_Display u_7_segment_display_2 (
    .g(Seg2[6]), .f(Seg2[5]), .a(Seg2[0]), .b(Seg2[1]), .e(Seg2[4]), .d(Seg2[3]), .c(Seg2[2]));  // open: dp
  J_K_Flip_Flop j_k_ff_4 (
    .J(1'b1), .clk(clock_1_out), .K(j_k_ff_3_qn), .Q(Q3), .Qn(j_k_ff_4_qn));  // open: preset, en, reset
  _7_Segment_Display u_7_segment_display_3 (
    .g(Seg3[6]), .f(Seg3[5]), .a(Seg3[0]), .b(Seg3[1]), .e(Seg3[4]), .d(Seg3[3]), .c(Seg3[2]));  // open: dp
  or or_1 (or_2_out[1], j_k_ff_4_qn, j_k_ff_3_qn);
  or or_2 (or_2_out[0], j_k_ff_4_qn, j_k_ff_2_qn);
  _7_Segment_Display u_7_segment_display_4 (
    .g(Seg4[6]), .f(Seg4[5]), .a(Seg4[0]), .b(Seg4[1]), .e(Seg4[4]), .d(Seg4[3]), .c(Seg4[2]));  // open: dp
  Multiplexer #(.select(2), .width(4), .enable("false")) multiplexer_1 (
    .in0(in_1), .in1(in_2), .in2(in_3), .in3(in_4), .out(multiplexer_1_out), .sel(or_2_out));
  Decoder_7_segmento__main main_1 (.in_1(multiplexer_1_out), .out_2(main_1_out_2));
  Multiplexer #(.width(7), .enable("false")) multiplexer_2 (.in0(main_1_out_2), .in1({7{1'b0}}), .out(Seg1), .sel(Q0));
  Multiplexer #(.width(7), .enable("false")) multiplexer_3 (.in0(main_1_out_2), .in1({7{1'b0}}), .out(Seg2), .sel(Q1));
  Multiplexer #(.width(7), .enable("false")) multiplexer_4 (.in0(main_1_out_2), .in1({7{1'b0}}), .out(Seg3), .sel(Q2));
  Multiplexer #(.width(7), .enable("false")) multiplexer_5 (.in0(main_1_out_2), .in1({7{1'b0}}), .out(Seg4), .sel(Q3));

  // Other names for the same wires on the sheet: D1[3:0] = in_1; D2[3:0] = in_2; D3[3:0] = in_3; D4[3:0] = in_4

  // Notes on the sheet:
  //   Decoder a 7 seg
endmodule
