// Logisim project Reloj Digital.circ as structural Verilog: 1 circuit, main circuit main
module main (
);

  wire clock_1_out, EN, ENH, J1, J1D, J1H, J2, J2D, J2H, J3, J3H, JE, K1, K1D, K1H, K2, K2H, K3H, KE, Q0N,
       Q0ND, Q0NH, Q1, Q1D, Q1N, Q1ND, Q1NH, Q2, Q2D, Q2H, Q2N, Q2ND, Q2NH, Q3, Q3D, Q3H, Q3N, Q3ND, Q3NH,
       QE, QEN;

  Clock clock_1 (.out(clock_1_out));
  and and_1 (EN, K1, Q1N, Q2N, Q3);
  and and_2 (ENH, K1, Q1N, Q2N, Q3, K1D, Q1ND, Q2D, Q3ND);
  J_K_Flip_Flop j_k_ff_1 (.J(1'b1), .clk(clock_1_out), .K(1'b1), .Q(K1), .Qn(Q0N));  // open: preset, en, reset
  J_K_Flip_Flop j_k_ff_2 (.J(1'b1), .clk(clock_1_out), .K(1'b1), .Q(K1D), .Qn(Q0ND), .en(EN));  // open: preset, reset
  J_K_Flip_Flop j_k_ff_3 (.J(1'b1), .clk(clock_1_out), .K(1'b1), .Q(K3H), .Qn(Q0NH), .en(ENH));  // open: preset, reset
  and and_3 (J1, Q3N, K1);
  J_K_Flip_Flop j_k_ff_4 (.J(J1), .clk(clock_1_out), .K(K1), .Q(Q1), .Qn(Q1N));  // open: preset, en, reset
  and and_4 (J1D, K1D, Q2ND);
  J_K_Flip_Flop j_k_ff_5 (.J(J1D), .clk(clock_1_out), .K(K1D), .Q(Q1D), .Qn(Q1ND), .en(EN));  // open: preset, reset
  and and_5 (J1H, Q3NH, K3H);
  J_K_Flip_Flop j_k_ff_6 (.J(J1H), .clk(clock_1_out), .K(K1H), .Q(KE), .Qn(Q1NH), .en(ENH));  // open: preset, reset
  or or_1 (K1H, QE, K3H);
  and and_6 (J2, K1, Q1);
  J_K_Flip_Flop j_k_ff_7 (.J(J2), .clk(clock_1_out), .K(K2), .Q(Q2), .Qn(Q2N));  // open: preset, en, reset
  and and_7 (K2, K1, Q1);
  and and_8 (J2D, K1D, Q1D);
  J_K_Flip_Flop j_k_ff_8 (.J(J2D), .clk(clock_1_out), .K(K1D), .Q(Q2D), .Qn(Q2ND), .en(EN));  // open: preset, reset
  and and_9 (J2H, K3H, KE);
  J_K_Flip_Flop j_k_ff_9 (.J(J2H), .clk(clock_1_out), .K(K2H), .Q(Q2H), .Qn(Q2NH), .en(ENH));  // open: preset, reset
  and and_10 (K2H, K3H, KE);
  and and_11 (J3, K1, Q1, Q2);
  J_K_Flip_Flop j_k_ff_10 (.J(J3), .clk(clock_1_out), .K(K1), .Q(Q3), .Qn(Q3N));  // open: preset, en, reset
  J_K_Flip_Flop j_k_ff_11 (.J(1'b0), .clk(clock_1_out), .K(1'b1), .Q(Q3D), .Qn(Q3ND), .en(EN));  // open: preset, reset
  and and_12 (J3H, K3H, KE, Q2H);
  J_K_Flip_Flop j_k_ff_12 (.J(J3H), .clk(clock_1_out), .K(K3H), .Q(Q3H), .Qn(Q3NH), .en(ENH));  // open: preset, reset
  DotMatrix #(.matrixcols(1), .matrixrows(1)) dotmatrix_1 (.col0(QE));
  and and_13 (JE, K3H, Q3H);
  DotMatrix #(.matrixcols(4), .matrixrows(1)) dotmatrix_2 (.col0(K3H), .col1(KE), .col2(Q2H), .col3(Q3H));
  J_K_Flip_Flop j_k_ff_13 (.J(JE), .clk(clock_1_out), .K(KE), .Q(QE), .Qn(QEN), .en(ENH));  // open: preset, reset
  DotMatrix #(.matrixcols(4), .matrixrows(1)) dotmatrix_3 (.col0(K1D), .col1(Q1D), .col2(Q2D), .col3(Q3D));
  DotMatrix #(.matrixcols(4), .matrixrows(1)) dotmatrix_4 (.col0(K1), .col1(Q1), .col2(Q2), .col3(Q3));

  // Other names for the same wires on the sheet: K3 = K1; Q0 = K1; K2D = K1D; Q0D = K1D; Q0H = K3H; Q1H = KE

  // Notes on the sheet:
  //   Hora
  //   :
  //   Minuto
endmodule
